// Logisim project cpu-harness.circ as structural Verilog: 1 circuit, main circuit main
module main (
  output [15:0] r0,
  output [15:0] r1,
  output [15:0] r2,
  output [15:0] r3,
  output [15:0] d0,
  output [15:0] d1,
  output [15:0] Data_Mem_Data,
  output [15:0] Data_Mem_Addr,
  output Write_Enabled,
  output [15:0] Clock_Count
);

  wire main_1_p5, main_1_p7;
  wire [15:0] adder_1_out, main_1_p10, main_1_p11, main_1_p12, ram_1_data;

  // Probe on main_1_p10
  // Probe on main_1_p7
  // Probe on ram_1_data
  RAM #(.addrWidth(16), .dataWidth(16)) ram_1 (.addr(main_1_p10), .data(ram_1_data));  // open: sel, clk, ld, clr
  // cpu_main main_1: pin names not known; wires that end beside it: ram_1_data, r0, r1, r2, main_1_p5, r3, main_1_p7, d0, d1, main_1_p10, main_1_p11, main_1_p12, Write_Enabled
  Multiplexer #(.width(16), .enable("false")) multiplexer_1 (
    .in0({16{1'b0}}), .in1(main_1_p11), .out(Data_Mem_Data), .sel(Write_Enabled));
  Multiplexer #(.width(16), .enable("false")) multiplexer_2 (
    .in0({16{1'b0}}), .in1(main_1_p12), .out(Data_Mem_Addr), .sel(Write_Enabled));
  Clock clock_1 (.out(main_1_p5));
  Register #(.width(16)) register_1 (.D(adder_1_out), .Q(Clock_Count), .clk(main_1_p5));  // open: en, clr
  Adder #(.width(16)) adder_1 (.a(16'h1), .b(Clock_Count), .out(adder_1_out));  // open: cin, cout

  // Notes on the sheet:
  //   Instruction Memory
  //   YOUR CPU SHOULD FIT OVER THERE
  //   There should be no blue/red wires here, and nothing should be x's.
  //   If you want to test your code, you can do it here by right clicking the RAM (Instruction Memory) and load image the appropriate hex file
endmodule
