// Logisim project cpu.circ as structural Verilog: 18 circuits, main circuit main
module main (
  input  [15:0] From_Instr_Mem,
  input  clk,
  output [15:0] r0,
  output [15:0] r1,
  output [15:0] r2,
  output [15:0] r3,
  output [15:0] Display_0,
  output [15:0] Display_1,
  output [15:0] To_Instr_Mem,
  output [15:0] Data_Mem_Data,
  output [15:0] Data_Mem_Addr,
  output Data_Mem_Write
);

  wire ALUSRC, bit_extender_3_out, demultiplexer_1_out0, demultiplexer_1_out1, DISP, EQUAL, EXT, JAL,
       main_2_signed_overflow, MEMR, NOOP, REGWR;
  wire [1:0] inst_1_rd, inst_1_rs, inst_1_rt, PC_SEL, REGDST;
  wire [3:0] CTR;
  wire [5:0] inst_1_func;
  wire [7:0] imm_1_out_3;
  wire [11:0] and_1_out;
  wire [15:0] bit_extender_1_out, bit_extender_2_out, IMM, JUMP, main_1_read_data_2, multiplexer_1_out,
       multiplexer_3_out, multiplexer_4_out, multiplexer_6_out, NPC, OFFSET, RESULT, RS;
  wire [15:12] register_1_q;

  Register #(.width(16)) PC (.D(multiplexer_3_out), .Q(To_Instr_Mem), .clk(clk));  // open: en, clr
  Adder #(.width(16)) adder_1 (.a(16'h1), .b(To_Instr_Mem), .out(NPC));  // open: cin, cout
  // Probe on NPC
  // Probe on multiplexer_1_out
  Register #(.width(16)) register_1 (
    .D(multiplexer_1_out), .Q({register_1_q, JUMP[11:0]}), .clk(clk));  // open: en, clr
  Multiplexer #(.select(2), .width(16)) multiplexer_1 (
    .in0(From_Instr_Mem), .in1({16{1'b0}}), .in2({16{1'b0}}), .in3({16{1'b0}}), .out(multiplexer_1_out),
    .sel(PC_SEL));  // open: en
  Adder #(.width(16)) adder_2 (.a(IMM), .b(To_Instr_Mem), .out(OFFSET));  // open: cin, cout
  assign {JUMP[15:12], and_1_out} = To_Instr_Mem & 16'hf000;  // AND_Gate and_1, 16 bits wide
  // Probe on {register_1_q, JUMP[11:0]}
  Control control_1 (
    .DISP(DISP), .Instruction({register_1_q, JUMP[11:0]}), .SRC(ALUSRC), .CTR(CTR), .EXT(EXT),
    .MEMW(Data_Mem_Write), .MEMR(MEMR), .REGW(REGWR), .REGD(REGDST), .JUMP(JAL), .NEXTPC_SEL(PC_SEL),
    .NOOP(NOOP), .EQUAL(EQUAL));
  INST inst_1 (
    .Instruction({register_1_q, JUMP[11:0]}), .RS(inst_1_rs), .RT(inst_1_rt), .RD(inst_1_rd),
    .FUNC(inst_1_func));  // open: OP
  IMM imm_1 (.TOP(inst_1_rd), .BOTTOM(inst_1_func), .out_3(imm_1_out_3));
  assign bit_extender_1_out = {{8{1'b0}}, imm_1_out_3};  // Bit_Extender bit_extender_1
  assign bit_extender_2_out = {{8{imm_1_out_3[7]}}, imm_1_out_3};  // Bit_Extender bit_extender_2
  // Probe on inst_1_rt
  // Probe on REGDST
  Multiplexer #(.width(16)) multiplexer_2 (
    .in0(bit_extender_1_out), .in1(bit_extender_2_out), .out(IMM), .sel(EXT));  // open: en
  Regfile_main main_1 (
    .Read_register_1(inst_1_rs), .Read_register_2(inst_1_rt), .write_register(REGDST), .write_data(RESULT),
    .Reg_0_Value(r0), .Reg_1_Value(r1), .Reg_2_Value(r2), .Reg_3_Value(r3), .RegWrite(REGWR), .clock(clk),
    .Read_Data_1(RS), .Read_Data_2(main_1_read_data_2));
  // Probe on IMM
  // Probe on NPC
  // Probe on JUMP
  // Probe on RS
  // Probe on OFFSET
  Multiplexer #(.select(2), .width(16)) multiplexer_3 (
    .in0(NPC), .in1(JUMP), .in2(RS), .in3(OFFSET), .out(multiplexer_3_out), .sel(PC_SEL));  // open: en
  // Probe on multiplexer_3_out
  Multiplexer #(.width(16)) multiplexer_4 (
    .in0(main_1_read_data_2), .in1(IMM), .out(multiplexer_4_out), .sel(ALUSRC));  // open: en
  LED led_1 (.in(main_2_signed_overflow));
  alu_main main_2 (
    .switch__S(CTR), .X(RS), .equal(EQUAL), .result(Data_Mem_Addr), .signed_overflow(main_2_signed_overflow),
    .Y(multiplexer_4_out));
  // Probe on To_Instr_Mem
  // Probe on RESULT
  Multiplexer #(.width(16)) multiplexer_5 (
    .in0(multiplexer_6_out), .in1(To_Instr_Mem), .out(RESULT), .sel(JAL));  // open: en
  // Probe on Data_Mem_Addr
  // Probe on multiplexer_6_out
  Multiplexer #(.width(16)) multiplexer_6 (
    .in0(Data_Mem_Addr), .in1(Data_Mem_Data), .out(multiplexer_6_out), .sel(MEMR));  // open: en
  // Probe on Data_Mem_Addr
  // Probe on Data_Mem_Data
  DATAMEM datamem_1 (
    .DataIn(main_1_read_data_2), .Address(Data_Mem_Addr), .DataOut(Data_Mem_Data), .MemWrite(Data_Mem_Write),
    .clk(clk));  // open: Reset
  Hex_Digit_Display hex_digit_display_1 (.value(Display_0[11:8]));  // open: dp
  Hex_Digit_Display hex_digit_display_2 (.value(Display_0[15:12]));  // open: dp
  // Probe on DISP
  Demultiplexer #(.enable("false")) demultiplexer_1 (
    .out0(demultiplexer_1_out0), .out1(demultiplexer_1_out1), .in(DISP), .sel(bit_extender_3_out));
  // Probe on Data_Mem_Addr
  // Probe on bit_extender_3_out
  Bit_Extender #(.in_width(16), .out_width(1)) bit_extender_3 (.in(Data_Mem_Addr), .out(bit_extender_3_out));
  Hex_Digit_Display hex_digit_display_3 (.value(Display_0[3:0]));  // open: dp
  Hex_Digit_Display hex_digit_display_4 (.value(Display_0[7:4]));  // open: dp
  // Probe on demultiplexer_1_out0
  // Probe on demultiplexer_1_out1
  Hex_Digit_Display hex_digit_display_5 (.value(Display_1[15:12]));  // open: dp
  Register #(.width(16)) register_2 (.D(RS), .en(demultiplexer_1_out0), .Q(Display_0), .clk(clk));  // open: clr
  Register #(.width(16)) register_3 (.D(RS), .en(demultiplexer_1_out1), .Q(Display_1), .clk(clk));  // open: clr
  Hex_Digit_Display hex_digit_display_6 (.value(Display_1[7:4]));  // open: dp
  Hex_Digit_Display hex_digit_display_7 (.value(Display_1[11:8]));  // open: dp
  // Probe on REGDST
  // Probe on REGWR
  // Probe on CTR
  // Probe on MEMR
  // Probe on Data_Mem_Write
  // Probe on EXT
  // Probe on ALUSRC
  // Probe on DISP
  // Probe on JAL
  // Probe on PC_SEL
  Hex_Digit_Display hex_digit_display_8 (.value(Display_1[3:0]));  // open: dp

  // Other names for the same wires on the sheet: d0[15:0] = Display_0; d1[15:0] = Display_1;
  //   D_n[15:0] = Data_Mem_Addr; MEMW = Data_Mem_Write; PC[15:0] = To_Instr_Mem

  // Notes on the sheet:
  //   This is the instruction that you would receive as INPUT
  //   This is the current PC that you need to send as OUTPUT
  //   This is a CLK that is an INPUT driven from the harness.
  //   Remember, this circuit is loaded from the harness to be tested!
  //   DO NOT CHANGE THE LOCATIONS OF THE INPUTS/OUTPUTS! IF YOU DO SO, YOU NEED TO MAKE SURE THE PINS ARE AT THE RIGHT PLACE!
  //   These are OUTPUTS to the circuit
  //   These are OUTPUTS to the circuit
  //   DISPLAY[0]
  //   DISPLAY[1]
endmodule

// DATA MEMORY
module DATAMEM (
  input  [15:0] DataIn,
  input  [15:0] Address,
  input  clk,
  input  Reset,
  input  MemWrite,
  output [15:0] DataOut
);

  wire not_1_out;

  assign DataOut = MemWrite ? DataIn : 16'bz;  // Controlled_Buffer controlled_buffer_1
  not not_1 (not_1_out, MemWrite);
  RAM #(.addrWidth(16), .dataWidth(16)) ram_1 (
    .addr(Address), .data(DataOut), .sel(1'b1), .clk(clk), .ld(not_1_out), .clr(Reset));
endmodule

module Output (
  input  [15:0] D0
);

  Hex_Digit_Display hex_digit_display_1 (.value(D0[11:8]));  // open: dp
  Hex_Digit_Display hex_digit_display_2 (.value(D0[15:12]));  // open: dp
  Hex_Digit_Display hex_digit_display_3 (.value(D0[3:0]));  // open: dp
  Hex_Digit_Display hex_digit_display_4 (.value(D0[7:4]));  // open: dp

  // Notes on the sheet:
  //   DISPLAY[0]
endmodule

// CONTROL
module Control (
  input  [15:0] Instruction,
  input  EQUAL,
  output DISP,
  output NOOP,
  output SRC,
  output [3:0] CTR,
  output EXT,
  output MEMW,
  output MEMR,
  output REGW,
  output [1:0] REGD,
  output JUMP,
  output [1:0] NEXTPC_SEL
);

  wire [1:0] inst_1_rd, inst_1_rs, inst_1_rt, inst_2_rd, inst_2_rs, inst_2_rt, inst_3_rd, inst_3_rs,
       inst_3_rt, inst_4_rd, inst_4_rs, inst_4_rt, inst_5_rd, inst_5_rs, inst_5_rt, inst_6_rd, inst_6_rs,
       inst_6_rt, inst_7_rd, inst_7_rs, inst_7_rt, inst_8_rd, inst_8_rs, inst_8_rt, inst_9_rd, inst_9_rs,
       inst_9_rt, inst_10_rd, inst_10_rs, inst_10_rt;
  wire [3:0] inst_1_op, inst_2_op, inst_3_op, inst_4_op, inst_5_op, inst_6_op, inst_7_op, inst_8_op,
       inst_9_op, inst_10_op;
  wire [5:0] inst_1_func, inst_2_func, inst_3_func, inst_4_func, inst_5_func, inst_6_func, inst_7_func,
       inst_8_func, inst_9_func, inst_10_func;

  NOOP noop_1 (.OUT(NOOP), .INST(Instruction));
  INST inst_1 (
    .Instruction(Instruction), .OP(inst_1_op), .RS(inst_1_rs), .RT(inst_1_rt), .RD(inst_1_rd),
    .FUNC(inst_1_func));
  INST inst_2 (
    .Instruction(Instruction), .OP(inst_2_op), .RS(inst_2_rs), .RT(inst_2_rt), .RD(inst_2_rd),
    .FUNC(inst_2_func));
  INST inst_3 (
    .Instruction(Instruction), .OP(inst_3_op), .RS(inst_3_rs), .RT(inst_3_rt), .RD(inst_3_rd),
    .FUNC(inst_3_func));
  INST inst_4 (
    .Instruction(Instruction), .OP(inst_4_op), .RS(inst_4_rs), .RT(inst_4_rt), .RD(inst_4_rd),
    .FUNC(inst_4_func));
  INST inst_5 (
    .Instruction(Instruction), .OP(inst_5_op), .RS(inst_5_rs), .RT(inst_5_rt), .RD(inst_5_rd),
    .FUNC(inst_5_func));
  INST inst_6 (
    .Instruction(Instruction), .OP(inst_6_op), .RS(inst_6_rs), .RT(inst_6_rt), .RD(inst_6_rd),
    .FUNC(inst_6_func));
  INST inst_7 (
    .Instruction(Instruction), .OP(inst_7_op), .RS(inst_7_rs), .RT(inst_7_rt), .RD(inst_7_rd),
    .FUNC(inst_7_func));
  INST inst_8 (
    .Instruction(Instruction), .OP(inst_8_op), .RS(inst_8_rs), .RT(inst_8_rt), .RD(inst_8_rd),
    .FUNC(inst_8_func));
  INST inst_9 (
    .Instruction(Instruction), .OP(inst_9_op), .RS(inst_9_rs), .RT(inst_9_rt), .RD(inst_9_rd),
    .FUNC(inst_9_func));
  INST inst_10 (
    .Instruction(Instruction), .OP(inst_10_op), .RS(inst_10_rs), .RT(inst_10_rt), .RD(inst_10_rd),
    .FUNC(inst_10_func));
  DISP disp_1 (.OPCODE(inst_1_op), .RS(inst_1_rs), .RT(inst_1_rt), .RD(inst_1_rd), .FUNC(inst_1_func), .OUT(DISP));
  ALUSRC alusrc_1 (.OPCODE(inst_2_op), .RS(inst_2_rs), .RT(inst_2_rt), .RD(inst_2_rd), .FUNC(inst_2_func), .OUT(SRC));
  ALUCTR aluctr_1 (.OPCODE(inst_3_op), .RS(inst_3_rs), .RT(inst_3_rt), .RD(inst_3_rd), .FUNC(inst_3_func), .OUT(CTR));
  EXTOP extop_1 (.OPCODE(inst_4_op), .RS(inst_4_rs), .RT(inst_4_rt), .RD(inst_4_rd), .FUNC(inst_4_func), .OUT(EXT));
  MEMWR memwr_1 (.OPCODE(inst_5_op), .RS(inst_5_rs), .RT(inst_5_rt), .RD(inst_5_rd), .FUNC(inst_5_func), .OUT(MEMW));
  MEMTOREG memtoreg_1 (
    .OPCODE(inst_6_op), .RS(inst_6_rs), .RT(inst_6_rt), .RD(inst_6_rd), .FUNC(inst_6_func), .OUT(MEMR));
  REGWRT regwrt_1 (.OPCODE(inst_7_op), .RS(inst_7_rs), .RT(inst_7_rt), .RD(inst_7_rd), .FUNC(inst_7_func), .OUT(REGW));
  REGDST regdst_1 (.OPCODE(inst_8_op), .RS(inst_8_rs), .RT(inst_8_rt), .RD(inst_8_rd), .FUNC(inst_8_func), .OUT(REGD));
  JR jr_1 (.OPCODE(inst_9_op), .RS(inst_9_rs), .RT(inst_9_rt), .RD(inst_9_rd), .FUNC(inst_9_func), .OUT(JUMP));
  NEXTPC_SEL nextpc_sel_1 (
    .OPCODE(inst_10_op), .RS(inst_10_rs), .RT(inst_10_rt), .RD(inst_10_rd), .FUNC(inst_10_func),
    .OUT(NEXTPC_SEL), .EQUAL(EQUAL));
endmodule

// SRC
module ALUSRC (
  input  [3:0] OPCODE,
  input  [1:0] RS,
  input  [1:0] RT,
  input  [1:0] RD,
  input  [5:0] FUNC,
  output OUT
);

  wire multiplexer_1_out, not_1_out, R;

  Comparator #(.width(4), .mode("unsigned")) comparator_1 (.a(OPCODE), .b(4'b0000), .eq(R));  // open: gt, lt
  // Probe on R
  Multiplexer #(.select(4)) multiplexer_1 (
    .in0(1'b0), .in1(1'b0), .in2(1'b0), .in3(1'b0), .in4(1'b1), .in5(1'b1), .in6(1'b1), .in7(1'b0),
    .in8(1'b0), .in9(1'b0), .in10(1'b0), .in11(1'b0), .in12(1'b1), .in13(1'b1), .in14(1'b1), .in15(1'b1),
    .out(multiplexer_1_out), .sel(OPCODE));  // open: en
  // Probe on multiplexer_1_out
  // Probe on OUT
  Multiplexer #(.disabled(0)) multiplexer_2 (
    .in0(1'b0), .in1(multiplexer_1_out), .out(OUT), .sel(not_1_out));  // open: en
  not not_1 (not_1_out, R);
  // Probe on not_1_out

  // Other names for the same wires on the sheet: OP[3:0] = OPCODE
endmodule

// CTR
module ALUCTR (
  input  [3:0] OPCODE,
  input  [1:0] RS,
  input  [1:0] RT,
  input  [1:0] RD,
  input  [5:0] FUNC,
  output [3:0] OUT
);

  wire not_1_out, R;
  wire [2:0] bit_extender_2_out;
  wire [3:0] bit_extender_1_out, multiplexer_1_out;

  Comparator #(.width(4), .mode("unsigned")) comparator_1 (.a(OPCODE), .b(4'b0000), .eq(R));  // open: gt, lt
  // Probe on R
  Multiplexer #(.select(4), .width(4)) multiplexer_1 (
    .in0(4'b0000), .in1(4'b1000), .in2(4'b1001), .in3(4'b1010), .in4(4'b0110), .in5(4'b0000), .in6(4'b0001),
    .in7(4'b0000), .in8(4'b0000), .in9(4'b0000), .in10(4'b0000), .in11(4'b0000), .in12(4'b0110),
    .in13(4'b1011), .in14(4'b0110), .in15(4'b1100), .out(multiplexer_1_out), .sel(OPCODE));  // open: en
  assign bit_extender_1_out = {{1{1'b0}}, bit_extender_2_out};  // Bit_Extender bit_extender_1
  Bit_Extender #(.in_width(6), .out_width(3)) bit_extender_2 (.in(FUNC), .out(bit_extender_2_out));
  // Probe on bit_extender_1_out
  // Probe on multiplexer_1_out
  // Probe on OUT
  Multiplexer #(.width(4), .disabled(0)) multiplexer_2 (
    .in0(bit_extender_1_out), .in1(multiplexer_1_out), .out(OUT), .sel(not_1_out));  // open: en
  not not_1 (not_1_out, R);
  // Probe on not_1_out

  // Other names for the same wires on the sheet: OP[3:0] = OPCODE
endmodule

// EXT
module EXTOP (
  input  [3:0] OPCODE,
  input  [1:0] RS,
  input  [1:0] RT,
  input  [1:0] RD,
  input  [5:0] FUNC,
  output OUT
);

  wire multiplexer_1_out, not_1_out, R;

  Comparator #(.width(4), .mode("unsigned")) comparator_1 (.a(OPCODE), .b(4'b0000), .eq(R));  // open: gt, lt
  // Probe on R
  Multiplexer #(.select(4)) multiplexer_1 (
    .in0(1'b0), .in1(1'b0), .in2(1'b0), .in3(1'b0), .in4(1'b1), .in5(1'b0), .in6(1'b0), .in7(1'b0),
    .in8(1'b0), .in9(1'b0), .in10(1'b1), .in11(1'b1), .in12(1'b1), .in13(1'b0), .in14(1'b1), .in15(1'b0),
    .out(multiplexer_1_out), .sel(OPCODE));  // open: en
  // Probe on multiplexer_1_out
  // Probe on OUT
  Multiplexer #(.disabled(0)) multiplexer_2 (
    .in0(1'b0), .in1(multiplexer_1_out), .out(OUT), .sel(not_1_out));  // open: en
  not not_1 (not_1_out, R);
  // Probe on not_1_out

  // Other names for the same wires on the sheet: OP[3:0] = OPCODE
endmodule

// MEMW
module MEMWR (
  input  [3:0] OPCODE,
  input  [1:0] RS,
  input  [1:0] RT,
  input  [1:0] RD,
  input  [5:0] FUNC,
  output OUT
);

  wire multiplexer_1_out, not_1_out, R;

  Comparator #(.width(4), .mode("unsigned")) comparator_1 (.a(OPCODE), .b(4'b0000), .eq(R));  // open: gt, lt
  // Probe on R
  Multiplexer #(.select(4)) multiplexer_1 (
    .in0(1'b0), .in1(1'b0), .in2(1'b0), .in3(1'b0), .in4(1'b0), .in5(1'b0), .in6(1'b0), .in7(1'b0),
    .in8(1'b0), .in9(1'b0), .in10(1'b0), .in11(1'b0), .in12(1'b1), .in13(1'b0), .in14(1'b0), .in15(1'b0),
    .out(multiplexer_1_out), .sel(OPCODE));  // open: en
  // Probe on multiplexer_1_out
  // Probe on OUT
  Multiplexer #(.disabled(0)) multiplexer_2 (
    .in0(1'b0), .in1(multiplexer_1_out), .out(OUT), .sel(not_1_out));  // open: en
  not not_1 (not_1_out, R);
  // Probe on not_1_out

  // Other names for the same wires on the sheet: OP[3:0] = OPCODE
endmodule

// MEMR
module MEMTOREG (
  input  [3:0] OPCODE,
  input  [1:0] RS,
  input  [1:0] RT,
  input  [1:0] RD,
  input  [5:0] FUNC,
  output OUT
);

  wire multiplexer_1_out, not_1_out, R;

  Comparator #(.width(4), .mode("unsigned")) comparator_1 (.a(OPCODE), .b(4'b0000), .eq(R));  // open: gt, lt
  // Probe on R
  Multiplexer #(.select(4)) multiplexer_1 (
    .in0(1'b0), .in1(1'b0), .in2(1'b0), .in3(1'b0), .in4(1'b0), .in5(1'b0), .in6(1'b0), .in7(1'b0),
    .in8(1'b0), .in9(1'b0), .in10(1'b0), .in11(1'b0), .in12(1'b0), .in13(1'b0), .in14(1'b1), .in15(1'b0),
    .out(multiplexer_1_out), .sel(OPCODE));  // open: en
  // Probe on multiplexer_1_out
  // Probe on OUT
  Multiplexer #(.disabled(0)) multiplexer_2 (
    .in0(1'b0), .in1(multiplexer_1_out), .out(OUT), .sel(not_1_out));  // open: en
  not not_1 (not_1_out, R);
  // Probe on not_1_out

  // Other names for the same wires on the sheet: OP[3:0] = OPCODE
endmodule

// REGW
module REGWRT (
  input  [3:0] OPCODE,
  input  [1:0] RS,
  input  [1:0] RT,
  input  [1:0] RD,
  input  [5:0] FUNC,
  output OUT
);

  wire multiplexer_1_out, not_1_out, R;

  Comparator #(.width(4), .mode("unsigned")) comparator_1 (.a(OPCODE), .b(4'b0000), .eq(R));  // open: gt, lt
  // Probe on R
  Multiplexer #(.select(4)) multiplexer_1 (
    .in0(1'b1), .in1(1'b1), .in2(1'b1), .in3(1'b1), .in4(1'b1), .in5(1'b1), .in6(1'b1), .in7(1'b1),
    .in8(1'b0), .in9(1'b0), .in10(1'b0), .in11(1'b0), .in12(1'b0), .in13(1'b1), .in14(1'b1), .in15(1'b0),
    .out(multiplexer_1_out), .sel(OPCODE));  // open: en
  // Probe on multiplexer_1_out
  // Probe on OUT
  Multiplexer #(.disabled(0)) multiplexer_2 (
    .in0(1'b1), .in1(multiplexer_1_out), .out(OUT), .sel(not_1_out));  // open: en
  not not_1 (not_1_out, R);
  // Probe on not_1_out

  // Other names for the same wires on the sheet: OP[3:0] = OPCODE
endmodule

// REGD
module REGDST (
  input  [3:0] OPCODE,
  input  [1:0] RS,
  input  [1:0] RT,
  input  [1:0] RD,
  input  [5:0] FUNC,
  output [1:0] OUT
);

  wire not_1_out, R;
  wire [1:0] multiplexer_1_out;

  Comparator #(.width(4), .mode("unsigned")) comparator_1 (.a(OPCODE), .b(4'b0000), .eq(R));  // open: gt, lt
  // Probe on R
  Multiplexer #(.select(4), .width(2)) multiplexer_1 (
    .in0(RT), .in1(RT), .in2(RT), .in3(RT), .in4(RT), .in5(RT), .in6(RT), .in7(2'b11), .in8(2'b00),
    .in9(2'b00), .in10(2'b00), .in11(2'b00), .in12(RT), .in13(RT), .in14(RT), .in15(2'b00),
    .out(multiplexer_1_out), .sel(OPCODE));  // open: en
  // Probe on RD
  // Probe on multiplexer_1_out
  // Probe on OUT
  Multiplexer #(.width(2), .disabled(0)) multiplexer_2 (
    .in0(RD), .in1(multiplexer_1_out), .out(OUT), .sel(not_1_out));  // open: en
  not not_1 (not_1_out, R);
  // Probe on not_1_out

  // Other names for the same wires on the sheet: OP[3:0] = OPCODE
endmodule

module INST (
  input  [15:0] Instruction,
  output [3:0] OP,
  output [1:0] RS,
  output [1:0] RT,
  output [1:0] RD,
  output [5:0] FUNC
);


  assign FUNC = Instruction[5:0];
  assign OP = Instruction[15:12];
  assign RD = Instruction[7:6];
  assign RS = Instruction[11:10];
  assign RT = Instruction[9:8];
endmodule

module IMM (
  input  [1:0] TOP,
  input  [5:0] BOTTOM,
  output [7:0] out_3
);


  assign out_3 = {TOP, BOTTOM};
endmodule

module JR (
  input  [3:0] OPCODE,
  input  [1:0] RS,
  input  [1:0] RT,
  input  [1:0] RD,
  input  [5:0] FUNC,
  output OUT
);

  wire multiplexer_1_out, not_1_out, R;

  Comparator #(.width(4), .mode("unsigned")) comparator_1 (.a(OPCODE), .b(4'b0000), .eq(R));  // open: gt, lt
  // Probe on R
  Multiplexer #(.select(4)) multiplexer_1 (
    .in0(1'b0), .in1(1'b0), .in2(1'b0), .in3(1'b0), .in4(1'b0), .in5(1'b0), .in6(1'b0), .in7(1'b1),
    .in8(1'b0), .in9(1'b0), .in10(1'b0), .in11(1'b0), .in12(1'b0), .in13(1'b0), .in14(1'b0), .in15(1'b0),
    .out(multiplexer_1_out), .sel(OPCODE));  // open: en
  // Probe on multiplexer_1_out
  // Probe on OUT
  Multiplexer #(.disabled(0)) multiplexer_2 (
    .in0(1'b0), .in1(multiplexer_1_out), .out(OUT), .sel(not_1_out));  // open: en
  not not_1 (not_1_out, R);
  // Probe on not_1_out

  // Other names for the same wires on the sheet: OP[3:0] = OPCODE
endmodule

// BRC
module BRANCH (
  input  [3:0] OPCODE,
  input  [1:0] RS,
  input  [1:0] RT,
  input  [1:0] RD,
  input  [5:0] FUNC,
  input  EQUAL,
  output OUT
);

  wire BR, multiplexer_2_out, R, xnor_1_out;

  Comparator #(.width(4), .mode("unsigned")) comparator_1 (.a(OPCODE), .b(4'b0000), .eq(R));  // open: gt, lt
  // Probe on R
  Multiplexer #(.select(4)) multiplexer_1 (
    .in0(1'b0), .in1(1'b0), .in2(1'b0), .in3(1'b0), .in4(1'b0), .in5(1'b0), .in6(1'b0), .in7(1'b0),
    .in8(1'b0), .in9(1'b0), .in10(1'b1), .in11(1'b1), .in12(1'b0), .in13(1'b0), .in14(1'b0), .in15(1'b0),
    .out(BR), .sel(OPCODE));  // open: en
  Multiplexer #(.select(4)) multiplexer_2 (
    .in0(1'b0), .in1(1'b0), .in2(1'b0), .in3(1'b0), .in4(1'b0), .in5(1'b0), .in6(1'b0), .in7(1'b0),
    .in8(1'b0), .in9(1'b0), .in10(1'b1), .in11(1'b0), .in12(1'b0), .in13(1'b0), .in14(1'b0), .in15(1'b0),
    .out(multiplexer_2_out), .sel(OPCODE));  // open: en
  xnor xnor_1 (xnor_1_out, multiplexer_2_out, EQUAL);
  // Probe on OUT
  Multiplexer #(.disabled(0)) multiplexer_3 (.in0(1'b0), .in1(xnor_1_out), .out(OUT), .sel(BR));  // open: en

  // Other names for the same wires on the sheet: OP[3:0] = OPCODE
endmodule

// NEXT
module NEXTPC_SEL (
  input  [3:0] OPCODE,
  input  [1:0] RS,
  input  [1:0] RT,
  input  [1:0] RD,
  input  [5:0] FUNC,
  input  EQUAL,
  output [1:0] OUT
);

  wire multiplexer_1_out, not_1_out, R, xnor_1_out;
  wire [1:0] multiplexer_2_out, multiplexer_3_out;

  Comparator #(.width(4), .mode("unsigned")) comparator_1 (.a(OPCODE), .b(4'b0000), .eq(R));  // open: gt, lt
  // Probe on R
  Multiplexer #(.select(4)) multiplexer_1 (
    .in0(1'b0), .in1(1'b0), .in2(1'b0), .in3(1'b0), .in4(1'b0), .in5(1'b0), .in6(1'b0), .in7(1'b0),
    .in8(1'b0), .in9(1'b0), .in10(1'b1), .in11(1'b0), .in12(1'b0), .in13(1'b0), .in14(1'b0), .in15(1'b0),
    .out(multiplexer_1_out), .sel(OPCODE));  // open: en
  xnor xnor_1 (xnor_1_out, multiplexer_1_out, EQUAL);
  Multiplexer #(.width(2)) multiplexer_2 (
    .in0(2'b00), .in1(2'b11), .out(multiplexer_2_out), .sel(xnor_1_out));  // open: en
  Multiplexer #(.select(4), .width(2)) multiplexer_3 (
    .in0(2'b00), .in1(2'b00), .in2(2'b00), .in3(2'b00), .in4(2'b00), .in5(2'b00), .in6(2'b00), .in7(2'b01),
    .in8(2'b01), .in9(2'b10), .in10(multiplexer_2_out), .in11(multiplexer_2_out), .in12(2'b00), .in13(2'b00),
    .in14(2'b00), .in15(2'b00), .out(multiplexer_3_out), .sel(OPCODE));  // open: en
  Multiplexer #(.width(2), .disabled(0)) multiplexer_4 (
    .in0(2'b00), .in1(multiplexer_3_out), .out(OUT), .sel(not_1_out));  // open: en
  not not_1 (not_1_out, R);
  // Probe on OUT
  // Probe on not_1_out

  // Other names for the same wires on the sheet: OP[3:0] = OPCODE
endmodule

module DISP (
  input  [3:0] OPCODE,
  input  [1:0] RS,
  input  [1:0] RT,
  input  [1:0] RD,
  input  [5:0] FUNC,
  output OUT
);

  wire multiplexer_1_out, not_1_out, R;

  Comparator #(.width(4), .mode("unsigned")) comparator_1 (.a(OPCODE), .b(4'b0000), .eq(R));  // open: gt, lt
  // Probe on R
  Multiplexer #(.select(4)) multiplexer_1 (
    .in0(1'b0), .in1(1'b0), .in2(1'b0), .in3(1'b0), .in4(1'b0), .in5(1'b0), .in6(1'b0), .in7(1'b0),
    .in8(1'b0), .in9(1'b0), .in10(1'b0), .in11(1'b0), .in12(1'b0), .in13(1'b0), .in14(1'b0), .in15(1'b1),
    .out(multiplexer_1_out), .sel(OPCODE));  // open: en
  // Probe on multiplexer_1_out
  // Probe on OUT
  Multiplexer #(.disabled(0)) multiplexer_2 (
    .in0(1'b0), .in1(multiplexer_1_out), .out(OUT), .sel(not_1_out));  // open: en
  not not_1 (not_1_out, R);
  // Probe on not_1_out

  // Other names for the same wires on the sheet: OP[3:0] = OPCODE
endmodule

module NOOP (
  input  [15:0] INST,
  output OUT
);

  Comparator #(.width(16)) comparator_1 (.a(INST), .b({16{1'b0}}), .eq(OUT));  // open: gt, lt
endmodule
