// Logisim project alu.circ as structural Verilog: 14 circuits, main circuit main
module main (
  input  [15:0] X,
  input  [15:0] Y,
  input  [3:0] switch__S,
  output signed_overflow,
  output [15:0] result,
  output equal
);

  wire add_1_overflow, and_2_out, and_3_out, demultiplexer_1_out7, demultiplexer_1_out8, sub_1_overflow;
  wire [15:0] ADD, AND, BC, FFO, LUI, OR, SLLV, SLT, SRAV, SRLV, SUB, ZB;

  AND and_1 (.Input_X(X), .Input_Y(Y), .out(AND));
  OR or_1 (.Input_X(X), .Input_Y(Y), .out(OR));
  SLT slt_1 (.Input_X(X), .Input_Y(Y), .out(SLT));
  SLLV sllv_1 (.Input_X(X), .Input_Y(Y), .out(SLLV));
  SRLV srlv_1 (.Input_X(X), .Input_Y(Y), .out(SRLV));
  SRAV srav_1 (.Input_X(X), .Input_Y(Y), .out(SRAV));
  ADD add_1 (.Input_X(X), .Input_Y(Y), .Overflow(add_1_overflow), .out(ADD));
  SUB sub_1 (.Input_X(X), .Input_Y(Y), .Overflow(sub_1_overflow), .out(SUB));
  EQUAL equal_1 (.Input_X(X), .Input_Y(Y), .out(equal));
  FFO ffo_1 (.Input_X(X), .out(FFO));
  ZB zb_1 (.Input_X(X), .out(ZB));
  BC bc_1 (.Input_X(X), .out(BC));
  LUI lui_1 (.Input_X(Y), .out(LUI));
  Demultiplexer #(.select(4)) demultiplexer_1 (
    .out7(demultiplexer_1_out7), .out8(demultiplexer_1_out8), .in(1'b1), .sel(switch__S));  // open: out0, out1, out2, out3, out4, out5, out6, out9, out10, out11, out12, out13, out14, out15, en
  and and_2 (and_2_out, demultiplexer_1_out7, add_1_overflow);
  or or_2 (signed_overflow, and_2_out, and_3_out);
  and and_3 (and_3_out, demultiplexer_1_out8, sub_1_overflow);
  Multiplexer #(.select(4), .width(16)) multiplexer_1 (
    .in0(AND), .in1(OR), .in2(SLT), .in3(SLLV), .in4(SRLV), .in5(SRAV), .in6(ADD), .in7(SUB), .in8(FFO),
    .in9(ZB), .in10(BC), .in11(LUI), .in12(Y), .out(result), .sel(switch__S));  // open: in13, in14, in15, en

  // Other names for the same wires on the sheet: DISP[15:0] = Y; OVERFLOW = signed_overflow; SELECT[3:0] = switch__S

  // Notes on the sheet:
  //   These are INPUTS to your circuit
  //   This is an INPUT to your circuit
  //   DO NOT CHANGE THE LOCATIONS OF THE INPUTS/OUTPUTS! IF YOU DO SO, YOU NEED TO MAKE SURE THE PINS ARE AT THE RIGHT PLACE!
  //   0
  //   1
  //   2
  //   3
  //   4
  //   5
  //   6
  //   7
  //   8
  //   9
  //   A
  //   B
  //   C
  //   These are OUTPUTS to your circuit
endmodule

module AND (
  input  [15:0] Input_X,
  input  [15:0] Input_Y,
  output [15:0] out
);

  assign out = Input_X & Input_Y;  // AND_Gate and_1, 16 bits wide
endmodule

module OR (
  input  [15:0] Input_X,
  input  [15:0] Input_Y,
  output [15:0] out
);

  assign out = Input_X | Input_Y;  // OR_Gate or_1, 16 bits wide
endmodule

module SLT (
  input  [15:0] Input_X,
  input  [15:0] Input_Y,
  output [15:0] out
);

  wire comparator_1_lt;

  Comparator #(.width(16)) comparator_1 (.a(Input_X), .b(Input_Y), .lt(comparator_1_lt));  // open: gt, eq
  assign out = {{15{1'b0}}, comparator_1_lt};  // Bit_Extender bit_extender_1
endmodule

module SLLV (
  input  [15:0] Input_X,
  input  [15:0] Input_Y,
  output [15:0] out
);

  wire [3:0] bit_extender_1_out;

  Bit_Extender #(.in_width(16), .out_width(4)) bit_extender_1 (.in(Input_Y), .out(bit_extender_1_out));
  Shifter #(.width(16)) shifter_1 (.in(Input_X), .\dist (bit_extender_1_out), .out(out));
endmodule

module SRLV (
  input  [15:0] Input_X,
  input  [15:0] Input_Y,
  output [15:0] out
);

  wire [3:0] bit_extender_1_out;

  Bit_Extender #(.in_width(16), .out_width(4)) bit_extender_1 (.in(Input_Y), .out(bit_extender_1_out));
  Shifter #(.width(16), .shift("lr")) shifter_1 (.in(Input_X), .\dist (bit_extender_1_out), .out(out));
endmodule

module SRAV (
  input  [15:0] Input_X,
  input  [15:0] Input_Y,
  output [15:0] out
);

  wire [3:0] bit_extender_1_out;

  Bit_Extender #(.in_width(16), .out_width(4)) bit_extender_1 (.in(Input_Y), .out(bit_extender_1_out));
  Shifter #(.width(16), .shift("ar")) shifter_1 (.in(Input_X), .\dist (bit_extender_1_out), .out(out));
endmodule

module ADD (
  input  [15:0] Input_X,
  input  [15:0] Input_Y,
  output Overflow,
  output [15:0] out
);

  wire comparator_1_eq, comparator_2_eq, not_1_out;

  // Probe on Input_X
  // Probe on Input_Y
  not not_1 (not_1_out, out[15]);
  Comparator #(.width(1)) comparator_1 (.a(Input_Y[15]), .b(Input_X[15]), .eq(comparator_1_eq));  // open: gt, lt
  Comparator #(.width(1)) comparator_2 (.a(Input_Y[15]), .b(not_1_out), .eq(comparator_2_eq));  // open: gt, lt
  Adder #(.width(16)) adder_1 (.a(Input_X), .b(Input_Y), .out(out));  // open: cin, cout
  // Probe on out
  and and_1 (Overflow, comparator_1_eq, comparator_2_eq);
endmodule

module SUB (
  input  [15:0] Input_X,
  input  [15:0] Input_Y,
  output Overflow,
  output [15:0] out
);

  wire comparator_1_eq, comparator_2_eq, or_1_out;

  // Probe on Input_X
  // Probe on Input_Y
  Comparator #(.width(1)) comparator_1 (.a(Input_X[15]), .b(Input_Y[15]), .eq(comparator_1_eq));  // open: gt, lt
  Comparator #(.width(1)) comparator_2 (.a(Input_X[15]), .b(out[15]), .eq(comparator_2_eq));  // open: gt, lt
  Subtractor #(.width(16)) subtractor_1 (.a(Input_X), .b(Input_Y), .out(out));  // open: bin, bout
  // Probe on out
  or or_1 (or_1_out, comparator_1_eq, comparator_2_eq);
  not not_1 (Overflow, or_1_out);
endmodule

module EQUAL (
  input  [15:0] Input_X,
  input  [15:0] Input_Y,
  output out
);

  Comparator #(.width(16)) comparator_1 (.a(Input_X), .b(Input_Y), .eq(out));  // open: gt, lt
endmodule

module ZB (
  input  [15:0] Input_X,
  output [15:0] out
);

  wire nor_1_out, nor_2_out, or_1_out, or_2_out, or_3_out, or_4_out, or_5_out;

  or or_1 (or_1_out, Input_X[0], Input_X[1], Input_X[2], Input_X[3]);
  or or_2 (or_2_out, Input_X[4], Input_X[5], Input_X[6], Input_X[7]);
  or or_3 (or_3_out, Input_X[8], Input_X[9], Input_X[10], Input_X[11]);
  or or_4 (or_4_out, Input_X[12], Input_X[13], Input_X[14], Input_X[15]);
  nor nor_1 (nor_1_out, or_1_out, or_2_out);
  nor nor_2 (nor_2_out, or_3_out, or_4_out);
  or or_5 (or_5_out, nor_1_out, nor_2_out);
  assign out = {{15{1'b0}}, or_5_out};  // Bit_Extender bit_extender_1
endmodule

module FFO (
  input  [15:0] Input_X,
  output [15:0] out
);

  wire bitfinder_1_found, not_1_out, undriven;
  wire [3:0] bitfinder_1_index;
  wire [15:0] bit_extender_1_out, subtractor_1_out;

  BitFinder #(.width(16), .\type ("high1")) bitfinder_1 (
    .in(Input_X), .index(bitfinder_1_index), .found(bitfinder_1_found));
  // Probe on bitfinder_1_index
  assign bit_extender_1_out = {{12{1'b0}}, bitfinder_1_index};  // Bit_Extender bit_extender_1
  not not_1 (not_1_out, bitfinder_1_found);
  // Probe on 16'hf
  Subtractor #(.width(16)) subtractor_1 (.a(16'hf), .b(bit_extender_1_out), .out(subtractor_1_out));  // open: bin, bout
  Multiplexer #(.width(16)) multiplexer_1 (
    .in0(subtractor_1_out), .in1(16'h10), .out(out), .sel(not_1_out), .en(undriven));
  // Probe on out
endmodule

module BC (
  input  [15:0] Input_X,
  output [15:0] out
);

  wire [4:0] bitadder_1_out;

  BitAdder #(.width(1)) bitadder_1 (
    .in0(Input_X[0]), .in1(Input_X[1]), .in2(Input_X[2]), .in3(Input_X[3]), .in4(Input_X[4]),
    .in5(Input_X[5]), .in6(Input_X[6]), .in7(Input_X[7]), .in8(Input_X[8]), .in9(Input_X[9]),
    .in10(Input_X[10]), .in11(Input_X[11]), .in12(Input_X[12]), .in13(Input_X[13]), .in14(Input_X[14]),
    .in15(Input_X[15]), .out(bitadder_1_out));
  assign out = {{11{1'b0}}, bitadder_1_out};  // Bit_Extender bit_extender_1
endmodule

module LUI (
  input  [15:0] Input_X,
  output [15:0] out
);

  Shifter #(.width(16)) shifter_1 (.in(Input_X), .\dist (4'b1000), .out(out));
endmodule
